# Fritzing sketch aqua-sensor-circuit (saved by Fritzing 0.9.3b)

parts:
  Part1 = Arduino Pro Mini v13
  Part2 = NRF24L01+ Breakout Board
  DS1 = DS18B20 1-Wire Temperature Sensor [part_number=DS18B20]
  J1 = female pin header, 3 pins [form="♀ (female)"]
  V1 = DC Power [voltage=3.3V]
  S1 = Reed switch [package=THT]
  J2 = female pin header, 4 pins [form="♀ (female)"]
  V2 = DC Power [voltage=5V]

nets:
  VCC: Part1.VCC, DS1.VDD, J1.pin1, V2.V+
  GND: Part1.GND, Part2.GND, DS1.GND, J1.pin3, V1.V-, S1.pin_2, V2.V-
  N1: Part1.D13/SCK, Part2.SCK
  N2: Part1.D12/MISO, Part2.MISO
  N3: Part1.D11_PWM/MOSI, Part2.MOSI
  N4: Part1.D10_PWM/SS, Part2.CS
  N5: Part1.D9_PWM, Part2.CE
  N6: Part1.D8, J2.pin1
  N7: Part1.D7, J2.pin2
  N8: Part1.D6_PWM, J2.pin3
  N9: Part1.D5_PWM, J2.pin4
  N10: Part1.D4, S1.pin_1
  N11: Part1.D3_PWM, J1.pin2
  N12: Part1.D2, DS1.DQ
  N13: Part2.VCC, V1.V+
